# Fritzing sketch MP1_Diagram (saved by Fritzing 0.9.5d)
breadboards: 1

parts:
  Arduino = Arduino Leonardo (Rev3b)
  LED1 = RGB LED (com. cathode, rgb) [package="5 mm [THT]"]
  S1 = SWITCH-MOMENTARY-2 [package=tactile-pth-12mm]
  R1 = Photocell (LDR) [package=THT]
  Lo-Fi_Variable_Resistor = TRIMPOT [package=3386u]
  Mic = Breakout Board for Electret Microphone
  R3 = Resistor [tolerance=±1% resistance=10k package="2010 [SMD]"]
  R4 = Resistor [tolerance=±1% resistance=220 package="2010 [SMD]"]
  R6 = Resistor [tolerance=±1% resistance=220 package="2010 [SMD]"]
  R5 = Resistor [tolerance=±1% resistance=220 package="2010 [SMD]"]

nets:
  N1: Arduino.D2/SDA, Arduino.SDA, S1.1
  N2: Arduino.D3_PWM/SCL, R4.Pin_0
  N3: Arduino.D5_PWM, R5.Pin_0
  N4: Arduino.D6_PWM/A7, R6.Pin_0
  3V3: Arduino.3V3, Mic.VCC
  N5: Arduino.5V, R1.pin_0, Lo-Fi_Variable_Resistor.CW
  N6: Arduino.A0, R1.pin_1, R3.Pin_0
  N7: Arduino.A1, Lo-Fi_Variable_Resistor.WIPER
  N8: Arduino.A2, Mic.AUD
  GND: Arduino.GND, LED1.common_cathode, S1.2, Lo-Fi_Variable_Resistor.CCW, Mic.GND, R3.Pin_1
  N9: LED1.red_anode, R4.Pin_1
  N10: LED1.green_anode, R5.Pin_1
  N11: LED1.blue_anode, R6.Pin_1
